// Logisim project mac.circ as structural Verilog: 2 circuits, main circuit main
module main (
);

  wire clk, not_1_out, rd_mem, rst;
  wire [15:0] counter_1_q, ld_a_16, ld_b_16, op1;
  wire [31:16] ram_256_32_dout;

  // DipSwitch #(.number(2)) switch: pin names not known; wires that end beside it: rd_mem, 1'b1
  Button u_rst (.out(rst));
  Clock clock_1 (.out(clk));
  // Probe on ld_b_16
  // Probe on ld_a_16
  RAM #(.addrWidth(16), .dataWidth(32)) ram_256_32 (
    .addr(counter_1_q), .we(not_1_out), .oe(rd_mem), .clk(clk), .din(32'ha000b),
    .dout({ram_256_32_dout, ld_a_16}));
  Counter #(.max('hffff), .width(16)) counter_1 (
    .load(1'b0), .D({16{1'b0}}), .count(1'b1), .Q(counter_1_q), .up(1'b1), .clk(clk), .clr(rst));  // open: carry
  not not_1 (not_1_out, rd_mem);
  // Probe on op1
  mac mac_1 (.a(ld_a_16), .b(ld_b_16), .clk(clk), .rst(rst), .op(op1));
  // Probe on ram_256_32_dout
  // Probe on ld_a_16
  Multiplexer #(.width(16)) multiplexer_1 (.in0(ram_256_32_dout), .in1(op1), .out(ld_b_16), .sel(1'b0));
endmodule

module mac (
  input  [15:0] a,
  input  [15:0] b,
  input  clk,
  input  rst,
  output [15:0] op
);

  wire not_1_out;
  wire [15:0] bit_extender_1_out, multiplexer_1_out, multiplexer_2_out, multiplier_1_out;

  assign bit_extender_1_out = {{15{1'b0}}, 1'b0};  // Bit_Extender bit_extender_1
  // Probe on a
  // Probe on b
  Multiplexer #(.width(16)) multiplexer_1 (.in0(bit_extender_1_out), .in1(a), .out(multiplexer_1_out), .sel(not_1_out));
  Multiplexer #(.width(16)) multiplexer_2 (.in0(bit_extender_1_out), .in1(b), .out(multiplexer_2_out), .sel(not_1_out));
  not not_1 (not_1_out, rst);
  // Probe on multiplier_1_out
  Multiplier #(.width(16)) multiplier_1 (
    .a(multiplexer_1_out), .b(multiplexer_2_out), .out(multiplier_1_out), .cin(op));  // open: cout
  // Probe on op
  Register #(.width(16)) register_1 (.D(multiplier_1_out), .en(1'b1), .clk(clk), .Q(op), .clr(rst));
endmodule
